// Logisim project MPU_RISC_4BITS.circ as structural Verilog: 3 circuits, main circuit main
module main (
);

  wire alu_1_overflow, alu_1_zero, CLOCK_out, not_1_out, not_2_out, OVR_q, RESET_out, uc_1_ac,
       \uc_1_direção , uc_1_ir, uc_1_load, \uc_1_modo_de_endereçamento , uc_1_pc, uc_1_r_w, uc_1_ram,
       uc_1_reset_out, Z_q;
  wire [2:0] uc_1_opcode;
  wire [3:0] AC_q, \alu_1_saída , multiplexer_1_out, PC_q, ram_1_data, \uc_1_endereço , uc_1_operando;
  wire [7:0] IR_q, rom_1_data;

  not not_1 (not_1_out, uc_1_load);
  UC uc_1 (
    .\Instrução (IR_q), .OpCode(uc_1_opcode), .\Modo_de_Endereçamento (\uc_1_modo_de_endereçamento ),
    .Operando(uc_1_operando), .IR(uc_1_ir), .PC(uc_1_pc), .AC(uc_1_ac), .RAM(uc_1_ram), .Clock(CLOCK_out),
    .Reset_In(RESET_out), .R_W(uc_1_r_w), .Z(Z_q), .C(OVR_q), .Load(uc_1_load), .\Endereço (\uc_1_endereço ),
    .Reset_Out(uc_1_reset_out), .\Direção (\uc_1_direção ));
  Button RESET (.out(RESET_out));
  Clock CLOCK (.out(CLOCK_out));
  ROM #(.addrWidth(4)) rom_1 (.addr(PC_q), .data(rom_1_data));  // open: sel
  Counter #(.width(4), .max('hf)) PC (
    .load(uc_1_load), .D(\uc_1_endereço ), .count(not_1_out), .Q(PC_q), .clk(uc_1_pc), .clr(uc_1_reset_out));  // open: carry
  // Probe on IR_q
  Register #(.trigger("high")) IR (.D(rom_1_data), .Q(IR_q), .clk(uc_1_ir));  // open: en, clr
  // Probe on AC_q
  // Probe on \uc_1_direção 
  // Probe on uc_1_opcode
  // Probe on multiplexer_1_out
  Multiplexer #(.width(4), .enable("false")) multiplexer_1 (
    .in0(uc_1_operando), .in1(ram_1_data), .out(multiplexer_1_out), .sel(\uc_1_modo_de_endereçamento ));
  ALU alu_1 (
    .\DIREÇÃO (\uc_1_direção ), .A(AC_q), .B(multiplexer_1_out), .ZERO(alu_1_zero),
    .OVERFLOW(alu_1_overflow), .\OPERAÇÃO (uc_1_opcode), .\SAÍDA (\alu_1_saída ));
  // Probe on \alu_1_saída 
  Register #(.width(4)) AC (.D(\alu_1_saída ), .Q(AC_q), .clk(uc_1_ac));  // open: en, clr
  RAM #(.addrWidth(4), .dataWidth(4)) ram_1 (
    .addr(uc_1_operando), .data(ram_1_data), .clk(uc_1_ram), .ld(uc_1_r_w));  // open: sel, clr
  assign ram_1_data = not_2_out ? AC_q : 4'bz;  // Controlled_Buffer controlled_buffer_1
  not not_2 (not_2_out, uc_1_r_w);
  Register #(.width(1)) Z (.D(alu_1_zero), .Q(Z_q), .clk(uc_1_ac));  // open: en, clr
  Register #(.width(1)) OVR (.D(alu_1_overflow), .Q(OVR_q), .clk(uc_1_ac));  // open: en, clr
  // Probe on AC_q

  // Notes on the sheet:
  //   MOV
  //   0
  //   1
  //   MOV
  //   ADD
  //   2
  //   3
  //   ADD
  //   SUB
  //   4
  //   5
  //   SUB
  //   6
  //   OR
  //   7
  //   OR
  //   NOT
  //   8
  //   NOT
  //   9
  //   A
  //   SHF
  //   B
  //   SHF
  //   C
  //   JPZ
  //   JPO
  //   D
  //   GO
  //   E
  //   STR
  //   F
  //   CONJUNTO DE INSTRUÇÕES
  //   0
  //   000
  //   AC <= X
  //   1
  //   000
  //   0
  //   001
  //   1
  //   001
  //   0
  //   010
  //   010
  //   1
  //   0
  //   011
  //   1
  //   011
  //   0
  //   100
  //   100
  //   1
  //   0
  //   101
  //   1
  //   101
  //   110
  //   0
  //   110
  //   1
  //   0
  //   111
  //   1
  //   111
  //   AC <= M(X)
  //   AC <= AC+X
  //   AC <= AC+M(X)
  //   AC <= AC-X
  //   AC <= AC-M(X)
  //   AC <= AC OR X
  //   AC <= AC OR M(X)
  //   AC <= NOT X
  //   AC <= NOT M( X)
  //   AC <= AC << Q
  //   AC <= AC >> Q
  //   PC <= X SE FLAG Z
  //   PC <= X SE FLAG O
  //   PC <= X
  //   M(X) <= AC 
  //   MEMÓRIA DE PROGRAMA
  //   contents of rom_1 (hex, n*v repeats v):
  //   0 f0 1 f1 10 31 d0 f2 11 f0 12 f1 e4
  //   PROCESSADOR RISC - 4 BITS
  //   MEMÓRIA DE DADOS
endmodule

module ALU (
  input  \DIREÇÃO ,
  input  [3:0] A,
  input  [3:0] B,
  input  [2:0] \OPERAÇÃO ,
  output OVERFLOW,
  output [3:0] \SAÍDA ,
  output ZERO
);

  wire adder_1_cout, and_1_out, and_2_out, decoder_1_out0, decoder_1_out1, decoder_1_out2, decoder_1_out3,
       decoder_1_out4, decoder_1_out5, decoder_1_out6, decoder_1_out7, not_2_out, subtractor_1_bout;
  wire [3:0] adder_1_out, controlled_buffer_6_out, not_1_out, or_2_out, shifter_1_out, shifter_2_out,
       subtractor_1_out;

  or or_1 (OVERFLOW, and_1_out, and_2_out);
  and and_1 (and_1_out, subtractor_1_bout, decoder_1_out2);
  and and_2 (and_2_out, adder_1_cout, decoder_1_out1);
  assign \SAÍDA  = decoder_1_out0 ? B : 4'bz;  // Controlled_Buffer controlled_buffer_1
  Decoder #(.select(3)) decoder_1 (
    .out0(decoder_1_out0), .out1(decoder_1_out1), .out2(decoder_1_out2), .out3(decoder_1_out3),
    .out4(decoder_1_out4), .out5(decoder_1_out5), .out6(decoder_1_out6), .out7(decoder_1_out7),
    .sel(\OPERAÇÃO ));  // open: en
  Adder #(.width(4)) adder_1 (.a(A), .b(B), .out(adder_1_out), .cout(adder_1_cout));  // open: cin
  Subtractor #(.width(4)) subtractor_1 (.a(A), .b(B), .out(subtractor_1_out), .bout(subtractor_1_bout));  // open: bin
  assign \SAÍDA  = decoder_1_out1 ? adder_1_out : 4'bz;  // Controlled_Buffer controlled_buffer_2
  nor nor_1 (ZERO, decoder_1_out7, decoder_1_out6, \SAÍDA [3], \SAÍDA [2], \SAÍDA [1], \SAÍDA [0]);
  assign not_1_out = ~B;  // NOT_Gate not_1, 4 bits wide
  assign or_2_out = A | B;  // OR_Gate or_2, 4 bits wide
  assign \SAÍDA  = decoder_1_out4 ? not_1_out : 4'bz;  // Controlled_Buffer controlled_buffer_3
  assign \SAÍDA  = decoder_1_out3 ? or_2_out : 4'bz;  // Controlled_Buffer controlled_buffer_4
  assign \SAÍDA  = decoder_1_out2 ? subtractor_1_out : 4'bz;  // Controlled_Buffer controlled_buffer_5
  assign controlled_buffer_6_out = \DIREÇÃO  ? shifter_1_out : 4'bz;  // Controlled_Buffer controlled_buffer_6
  Shifter #(.width(4), .shift("lr")) shifter_1 (.in(A), .\dist (B[1:0]), .out(shifter_1_out));
  Shifter #(.width(4)) shifter_2 (.in(A), .\dist (B[1:0]), .out(shifter_2_out));
  assign controlled_buffer_6_out = not_2_out ? shifter_2_out : 4'bz;  // Controlled_Buffer controlled_buffer_7
  not not_2 (not_2_out, \DIREÇÃO );
  assign \SAÍDA  = decoder_1_out5 ? controlled_buffer_6_out : 4'bz;  // Controlled_Buffer controlled_buffer_8
endmodule

module UC (
  input  [7:0] \Instrução ,
  input  Clock,
  input  Reset_In,
  input  C,
  input  Z,
  output Reset_Out,
  output IR,
  output PC,
  output AC,
  output RAM,
  output [3:0] \Endereço ,
  output [3:0] Operando,
  output \Direção ,
  output Load,
  output R_W,
  output [2:0] OpCode,
  output \Modo_de_Endereçamento 
);

  wire GOTO_out, JC_out, JZ_out, nand_1_out;
  wire [1:0] counter_1_q;

  Counter #(.width(2), .max('h3)) counter_1 (
    .Q(counter_1_q), .clk(Clock), .clr(Reset_In));  // open: load, D, count, carry
  and GOTO (GOTO_out, \Instrução [7], \Instrução [6], \Instrução [5], ~\Instrução [4], IR);  // AND_Gate
  and and_1 (AC, counter_1_q[1], ~counter_1_q[0]);  // AND_Gate
  and and_2 (IR, ~counter_1_q[1], ~counter_1_q[0]);  // AND_Gate
  and and_3 (PC, ~counter_1_q[1], counter_1_q[0]);  // AND_Gate
  and JC (JC_out, \Instrução [7], \Instrução [6], ~\Instrução [5], \Instrução [4], C, IR);  // AND_Gate
  or or_1 (Load, GOTO_out, JC_out, JZ_out);
  and and_4 (RAM, counter_1_q[1], counter_1_q[0]);
  and JZ (JZ_out, \Instrução [7], \Instrução [6], ~\Instrução [5], ~\Instrução [4], Z, IR);  // AND_Gate
  nand u_R_W (R_W, AC, \Instrução [4], \Instrução [5], \Instrução [6], \Instrução [7]);
  nand nand_1 (nand_1_out, \Instrução [7], ~\Instrução [6], \Instrução [5], \Instrução [4]);  // NAND_Gate
  and and_5 (\Modo_de_Endereçamento , \Instrução [4], nand_1_out);

  assign \Direção  = \Instrução [4];
  assign \Endereço  = \Instrução [3:0];
  assign OpCode = \Instrução [7:5];
  assign Operando = \Instrução [3:0];
  assign Reset_Out = Reset_In;
endmodule
